// Logisim project chain_selector.circ as structural Verilog: 2 circuits, main circuit main
module main (
  input  in_1,
  input  in_2,
  input  in_3,
  input  in_4,
  input  in_5,
  input  in_6,
  input  in_7,
  input  in_8,
  input  in_9,
  output out_10,
  output out_11,
  output out_12,
  output out_13,
  output out_14,
  output out_15,
  output out_16,
  output out_17,
  output out_18
);

  wire chain_selector_1_p8, chain_selector_1_p9, chain_selector_1_p10, chain_selector_2_out_8,
       chain_selector_2_out_9, chain_selector_2_out_10, chain_selector_3_out_8, chain_selector_3_out_9,
       chain_selector_3_out_10, chain_selector_4_out_8, chain_selector_4_out_9, chain_selector_4_out_10,
       chain_selector_5_out_8, chain_selector_5_out_9, chain_selector_5_out_10, chain_selector_6_out_8,
       chain_selector_6_out_9, chain_selector_6_out_10, chain_selector_7_out_8, chain_selector_7_out_9,
       chain_selector_7_out_10, clock_1_out;
  wire [2:0] chain_selector_1_p11, chain_selector_1_p12, chain_selector_1_p13, chain_selector_1_p14,
       chain_selector_2_out_11, chain_selector_2_out_12, chain_selector_2_out_13, chain_selector_2_out_14,
       chain_selector_3_out_11, chain_selector_3_out_12, chain_selector_3_out_13, chain_selector_3_out_14,
       chain_selector_4_out_11, chain_selector_4_out_12, chain_selector_4_out_13, chain_selector_4_out_14,
       chain_selector_5_out_11, chain_selector_5_out_12, chain_selector_5_out_13, chain_selector_5_out_14,
       chain_selector_6_out_11, chain_selector_6_out_12, chain_selector_6_out_13, chain_selector_6_out_14,
       chain_selector_7_out_11, chain_selector_7_out_12, chain_selector_7_out_13, chain_selector_7_out_14;
  wire [7:0] rom_1_data;
  wire [23:0] counter_1_q;

  ROM #(.addrWidth(24)) rom_1 (.addr(counter_1_q), .data(rom_1_data));
  Counter #(.width(24), .max('hffffff)) counter_1 (
    .up(clock_1_out), .clk(clock_1_out), .Q(counter_1_q));  // open: clr, load, count, D, carry
  Clock clock_1 (.out(clock_1_out));
  // chain_selector chain_selector_1: pin names not known; wires that end beside it: rom_1_data[0], rom_1_data[1], rom_1_data[2], rom_1_data[3], rom_1_data[4], rom_1_data[5], rom_1_data[6], chain_selector_1_p8, chain_selector_1_p9, chain_selector_1_p10, chain_selector_1_p11, chain_selector_1_p12, chain_selector_1_p13, chain_selector_1_p14
  chain_selector chain_selector_2 (
    .B(chain_selector_7_out_8), .CLK(chain_selector_7_out_9), .RESET(chain_selector_7_out_10),
    .in_4(chain_selector_7_out_11), .in_5(chain_selector_7_out_12), .in_6(chain_selector_7_out_13),
    .in_7(chain_selector_7_out_14), .out_8(chain_selector_2_out_8), .out_9(chain_selector_2_out_9),
    .out_10(chain_selector_2_out_10), .out_11(chain_selector_2_out_11), .out_12(chain_selector_2_out_12),
    .out_13(chain_selector_2_out_13), .out_14(chain_selector_2_out_14));
  chain_selector chain_selector_3 (
    .B(chain_selector_1_p8), .CLK(chain_selector_1_p9), .RESET(chain_selector_1_p10),
    .in_4(chain_selector_1_p11), .in_5(chain_selector_1_p12), .in_6(chain_selector_1_p13),
    .in_7(chain_selector_1_p14), .out_8(chain_selector_3_out_8), .out_9(chain_selector_3_out_9),
    .out_10(chain_selector_3_out_10), .out_11(chain_selector_3_out_11), .out_12(chain_selector_3_out_12),
    .out_13(chain_selector_3_out_13), .out_14(chain_selector_3_out_14));
  chain_selector chain_selector_4 (
    .B(chain_selector_2_out_8), .CLK(chain_selector_2_out_9), .RESET(chain_selector_2_out_10),
    .in_4(chain_selector_2_out_11), .in_5(chain_selector_2_out_12), .in_6(chain_selector_2_out_13),
    .in_7(chain_selector_2_out_14), .out_8(chain_selector_4_out_8), .out_9(chain_selector_4_out_9),
    .out_10(chain_selector_4_out_10), .out_11(chain_selector_4_out_11), .out_12(chain_selector_4_out_12),
    .out_13(chain_selector_4_out_13), .out_14(chain_selector_4_out_14));
  chain_selector chain_selector_5 (
    .B(chain_selector_3_out_8), .CLK(chain_selector_3_out_9), .RESET(chain_selector_3_out_10),
    .in_4(chain_selector_3_out_11), .in_5(chain_selector_3_out_12), .in_6(chain_selector_3_out_13),
    .in_7(chain_selector_3_out_14), .out_8(chain_selector_5_out_8), .out_9(chain_selector_5_out_9),
    .out_10(chain_selector_5_out_10), .out_11(chain_selector_5_out_11), .out_12(chain_selector_5_out_12),
    .out_13(chain_selector_5_out_13), .out_14(chain_selector_5_out_14));
  chain_selector chain_selector_6 (
    .B(chain_selector_4_out_8), .CLK(chain_selector_4_out_9), .RESET(chain_selector_4_out_10),
    .in_4(chain_selector_4_out_11), .in_5(chain_selector_4_out_12), .in_6(chain_selector_4_out_13),
    .in_7(chain_selector_4_out_14), .out_8(chain_selector_6_out_8), .out_9(chain_selector_6_out_9),
    .out_10(chain_selector_6_out_10), .out_11(chain_selector_6_out_11), .out_12(chain_selector_6_out_12),
    .out_13(chain_selector_6_out_13), .out_14(chain_selector_6_out_14));
  chain_selector chain_selector_7 (
    .B(chain_selector_5_out_8), .CLK(chain_selector_5_out_9), .RESET(chain_selector_5_out_10),
    .in_4(chain_selector_5_out_11), .in_5(chain_selector_5_out_12), .in_6(chain_selector_5_out_13),
    .in_7(chain_selector_5_out_14), .out_8(chain_selector_7_out_8), .out_9(chain_selector_7_out_9),
    .out_10(chain_selector_7_out_10), .out_11(chain_selector_7_out_11), .out_12(chain_selector_7_out_12),
    .out_13(chain_selector_7_out_13), .out_14(chain_selector_7_out_14));
  chain_selector chain_selector_8 (
    .B(chain_selector_6_out_8), .CLK(chain_selector_6_out_9), .RESET(chain_selector_6_out_10),
    .in_4(chain_selector_6_out_11), .in_5(chain_selector_6_out_12), .in_6(chain_selector_6_out_13),
    .in_7(chain_selector_6_out_14));  // open: out_8, out_9, out_10, out_11, out_12, out_13, out_14
endmodule

module chain_selector (
  input  B,
  input  CLK,
  input  RESET,
  input  [2:0] in_4,
  input  [2:0] in_5,
  input  [2:0] in_6,
  input  [2:0] in_7,
  output out_8,
  output out_9,
  output out_10,
  output [2:0] out_11,
  output [2:0] out_12,
  output [2:0] out_13,
  output [2:0] out_14
);

  wire and_1_out, register_1_q;

  Register #(.width(1)) register_1 (.D(B), .clk(CLK), .Q(register_1_q), .clr(and_1_out));  // open: en
  and and_1 (and_1_out, CLK, RESET);
  and and_2 (out_8, register_1_q, B);

  assign out_9 = CLK;
  assign out_10 = RESET;
  assign out_11 = in_4;
  assign out_12 = in_5;
  assign out_13 = in_6;
  assign out_14 = in_7;
endmodule
