// Logisim project fpga.circ as structural Verilog: 17 circuits, main circuit dissipation_zone
module main (
  input  [3:0] in_1,
  input  A,
  input  B,
  input  in_4,
  input  in_5,
  output out_6
);

  wire and2_1_out_3, and2_2_out_3, and2_3_out_3, and2_4_out_3, button_1_out, chain_selector3_1_cso,
       chain_selector3_1_ity, chain_selector3_2_cso, chain_selector3_2_ity, not_1_out, not_2_out;
  wire [3:0] register_1_q;

  Button button_1 (.out(button_1_out));
  not not_1 (not_1_out, A);
  not not_2 (not_2_out, B);
  and2 and2_1 (.in_1(not_1_out), .in_2(not_2_out), .out_3(and2_1_out_3));
  and2 and2_2 (.in_1(not_1_out), .in_2(B), .out_3(and2_2_out_3));
  and2 and2_3 (.in_1(A), .in_2(not_2_out), .out_3(and2_3_out_3));
  and2 and2_4 (.in_1(A), .in_2(B), .out_3(and2_4_out_3));
  Register #(.width(4)) register_1 (.D(in_1), .clk(button_1_out), .Q(register_1_q));  // open: en, clr
  sigif sigif_1 (.sig(register_1_q[3]), .cond(and2_1_out_3), .out_3(out_6));
  sigif sigif_2 (.sig(register_1_q[2]), .cond(and2_2_out_3), .out_3(out_6));
  sigif sigif_3 (.sig(register_1_q[1]), .cond(and2_3_out_3), .out_3(out_6));
  sigif sigif_4 (.sig(register_1_q[0]), .cond(and2_4_out_3), .out_3(out_6));
  chain_selector3 chain_selector3_1 (
    .CS(in_4), .ITM(in_5), .CSO(chain_selector3_1_cso), .ITY(chain_selector3_1_ity));  // open: CSR, CSRO
  chain_selector3 chain_selector3_2 (
    .CS(chain_selector3_1_cso), .ITM(chain_selector3_1_ity), .CSO(chain_selector3_2_cso),
    .ITY(chain_selector3_2_ity));  // open: CSR, CSRO
  chain_selector3 chain_selector3_3 (
    .CS(chain_selector3_2_cso), .ITM(chain_selector3_2_ity));  // open: CSR, CSO, ITY, CSRO

  // Notes on the sheet:
  //   A0 B0
  //   A0 B1
  //   A1 B0
  //   A1 B1
endmodule

module dissipation_zone (
  input  in_1,
  output out_2
);

  wire transistor_1_out, transistor_2_out, transistor_3_out, transistor_4_out;

  Transistor #(.\type ("n"), .gate("br")) transistor_1 (.in(1'b1), .out(transistor_1_out), .gate(in_1));
  Transistor #(.\type ("n"), .gate("br")) transistor_2 (.in(1'b1), .out(transistor_2_out), .gate(in_1));
  Transistor transistor_3 (.in(1'b0), .out(transistor_3_out), .gate(in_1));
  Transistor transistor_4 (.in(1'b0), .out(transistor_4_out), .gate(in_1));
  Transistor #(.\type ("n"), .gate("br")) transistor_5 (.in(transistor_1_out), .out(out_2), .gate(transistor_2_out));
  Transistor transistor_6 (.in(transistor_4_out), .out(out_2), .gate(transistor_3_out));
endmodule

module inv (
  input  in_1,
  output out_2
);

  wire transistor_1_out, transistor_2_out, transistor_3_out, transistor_4_out;

  Transistor #(.gate("br")) transistor_1 (.in(1'b1), .out(transistor_1_out), .gate(in_1));
  Transistor #(.gate("br")) transistor_2 (.in(1'b1), .out(transistor_2_out), .gate(in_1));
  Transistor #(.\type ("n")) transistor_3 (.in(1'b0), .out(transistor_3_out), .gate(in_1));
  Transistor #(.\type ("n")) transistor_4 (.in(1'b0), .out(transistor_4_out), .gate(in_1));
  Transistor #(.\type ("n"), .gate("br")) transistor_5 (.in(transistor_1_out), .out(out_2), .gate(transistor_2_out));
  Transistor transistor_6 (.in(transistor_4_out), .out(out_2), .gate(transistor_3_out));
endmodule

module sig_sel (
  input  in_1,
  input  in_2,
  input  in_3,
  output out_4
);

  wire transistor_1_out, transistor_2_out, transistor_3_out, transistor_4_out;

  Transistor #(.\type ("n"), .gate("br")) transistor_1 (.in(in_1), .out(transistor_1_out), .gate(in_2));
  Transistor #(.\type ("n"), .gate("br")) transistor_2 (.in(in_2), .out(transistor_2_out), .gate(in_2));
  Transistor transistor_3 (.in(in_2), .out(transistor_3_out), .gate(in_2));
  Transistor transistor_4 (.in(in_3), .out(transistor_4_out), .gate(in_2));
  Transistor #(.\type ("n"), .gate("br")) transistor_5 (.in(transistor_1_out), .out(out_4), .gate(transistor_2_out));
  Transistor transistor_6 (.in(transistor_4_out), .out(out_4), .gate(transistor_3_out));
endmodule

module and2 (
  input  in_1,
  input  in_2,
  output out_3
);

  wire transistor_1_out, transistor_2_out, transistor_3_out, transistor_4_out;

  Transistor #(.\type ("n"), .gate("br")) transistor_1 (.in(in_1), .out(transistor_1_out), .gate(in_2));
  Transistor #(.\type ("n"), .gate("br")) transistor_2 (.in(in_2), .out(transistor_2_out), .gate(in_2));
  Transistor transistor_3 (.in(in_2), .out(transistor_3_out), .gate(in_2));
  Transistor transistor_4 (.in(in_2), .out(transistor_4_out), .gate(in_2));
  Transistor #(.\type ("n"), .gate("br")) transistor_5 (.in(transistor_1_out), .out(out_3), .gate(transistor_2_out));
  Transistor transistor_6 (.in(transistor_4_out), .out(out_3), .gate(transistor_3_out));
endmodule

module or2 (
  input  in_1,
  input  in_2,
  output out_3
);

  wire transistor_1_out, transistor_2_out, transistor_3_out, transistor_4_out;

  Transistor #(.\type ("n"), .gate("br")) transistor_1 (.in(in_1), .out(transistor_1_out), .gate(in_1));
  Transistor #(.\type ("n"), .gate("br")) transistor_2 (.in(in_1), .out(transistor_2_out), .gate(in_1));
  Transistor transistor_3 (.in(in_1), .out(transistor_3_out), .gate(in_1));
  Transistor transistor_4 (.in(in_2), .out(transistor_4_out), .gate(in_1));
  Transistor #(.\type ("n"), .gate("br")) transistor_5 (.in(transistor_1_out), .out(out_3), .gate(transistor_2_out));
  Transistor transistor_6 (.in(transistor_4_out), .out(out_3), .gate(transistor_3_out));
endmodule

module xor2 (
  input  a,
  input  b,
  output out_3
);

  wire and2_1_out_3, inv_1_out_2, or2_1_out_3;

  or2 or2_1 (.in_1(a), .in_2(b), .out_3(or2_1_out_3));
  and2 and2_1 (.in_1(a), .in_2(b), .out_3(and2_1_out_3));
  inv inv_1 (.in_1(and2_1_out_3), .out_2(inv_1_out_2));
  and2 and2_2 (.in_1(or2_1_out_3), .in_2(inv_1_out_2), .out_3(out_3));
endmodule

module nand2 (
  input  in_1,
  input  in_2,
  output out_3
);

  wire and2_1_out_3;

  and2 and2_1 (.in_1(in_1), .in_2(in_2), .out_3(and2_1_out_3));
  inv inv_1 (.in_1(and2_1_out_3), .out_2(out_3));
endmodule

module nor2 (
  input  in_1,
  input  in_2,
  output out_3
);

  wire or2_1_out_3;

  inv inv_1 (.in_1(or2_1_out_3), .out_2(out_3));
  or2 or2_1 (.in_1(in_1), .in_2(in_2), .out_3(or2_1_out_3));
endmodule

module nxor2 (
  input  in_1,
  input  in_2,
  output out_3
);

  wire xor2_1_out_3;

  xor2 xor2_1 (.a(in_1), .b(in_2), .out_3(xor2_1_out_3));
  inv inv_1 (.in_1(xor2_1_out_3), .out_2(out_3));
endmodule

module sigif (
  input  sig,
  input  cond,
  output out_3
);

  wire transistor_1_out, transistor_2_out;

  Transistor #(.\type ("n"), .gate("br")) transistor_1 (.in(sig), .out(transistor_1_out), .gate(cond));
  Transistor #(.\type ("n"), .gate("br")) transistor_2 (.in(cond), .out(transistor_2_out), .gate(cond));
  Transistor #(.\type ("n"), .gate("br")) transistor_3 (.in(transistor_1_out), .out(out_3), .gate(transistor_2_out));
endmodule

module boolean_function (
  input  [3:0] f,
  input  f_we,
  input  f_set,
  input  f_reset,
  input  a,
  input  b,
  output out_7
);

  wire and2_1_out_3, and2_2_out_3, and2_3_out_3, and2_4_out_3, inv_1_out_2, not_1_out, not_2_out;
  wire [3:0] register_1_q;

  not not_1 (not_1_out, a);
  not not_2 (not_2_out, b);
  inv inv_1 (.in_1(f_we), .out_2(inv_1_out_2));
  and2 and2_1 (.in_1(not_1_out), .in_2(not_2_out), .out_3(and2_1_out_3));
  and2 and2_2 (.in_1(not_1_out), .in_2(b), .out_3(and2_2_out_3));
  and2 and2_3 (.in_1(a), .in_2(not_2_out), .out_3(and2_3_out_3));
  and2 and2_4 (.in_1(a), .in_2(b), .out_3(and2_4_out_3));
  Register #(.width(4)) register_1 (.D(f), .en(inv_1_out_2), .clk(f_set), .Q(register_1_q), .clr(f_reset));
  sigif sigif_1 (.sig(register_1_q[3]), .cond(and2_1_out_3), .out_3(out_7));
  sigif sigif_2 (.sig(register_1_q[2]), .cond(and2_2_out_3), .out_3(out_7));
  sigif sigif_3 (.sig(register_1_q[1]), .cond(and2_3_out_3), .out_3(out_7));
  sigif sigif_4 (.sig(register_1_q[0]), .cond(and2_4_out_3), .out_3(out_7));

  // Notes on the sheet:
  //   A0 B0
  //   A0 B1
  //   A1 B0
  //   A1 B1
endmodule

module chain_selector3 (
  input  CS,
  input  ITM,
  input  CSR,
  output CSO,
  output ITY,
  output CSRO
);

  wire inv_1_out_2, register_1_q;

  Register #(.width(1)) register_1 (.D(inv_1_out_2), .clk(inv_1_out_2), .Q(register_1_q), .clr(CSR));  // open: en
  inv inv_1 (.in_1(CS), .out_2(inv_1_out_2));
  and2 and2_1 (.in_1(CS), .in_2(register_1_q), .out_3(CSO));

  assign CSRO = CSR;
  assign ITY = ITM;
endmodule

module fpga_cell2 (
  input  A,
  input  B,
  input  C,
  input  [7:0] F,
  input  CS,
  input  ITM,
  input  CSR,
  output [7:0] FO,
  output R,
  output CSO,
  output ITY,
  output CSRO
);

  wire and2_1_out_3;
  wire [7:0] transistor_1_out;

  and2 and2_1 (.in_1(CS), .in_2(ITM), .out_3(and2_1_out_3));
  Transistor #(.gate("br"), .width(8)) transistor_1 (.in(F), .out(transistor_1_out), .gate(and2_1_out_3));
  boolean_function3 boolean_function3_1 (
    .in_1(transistor_1_out), .A(A), .B(B), .C(C), .out_8(R));  // open: in_2, in_3, in_4
  chain_selector3 chain_selector3_1 (.CS(CS), .ITM(ITM), .CSR(CSR), .CSO(CSO), .ITY(ITY), .CSRO(CSRO));

  assign FO = F;
endmodule

module boolean_function3 (
  input  [7:0] in_1,
  input  in_2,
  input  in_3,
  input  in_4,
  input  A,
  input  B,
  input  C,
  output out_8
);

  wire and2_1_out_3, and2_2_out_3, and2_3_out_3, and2_4_out_3, and2_5_out_3, and2_6_out_3, and2_7_out_3,
       and2_8_out_3, and2_9_out_3, and2_10_out_3, and2_11_out_3, and2_12_out_3, and2_13_out_3, and2_14_out_3,
       and2_15_out_3, and2_16_out_3, inv_1_out_2, not_1_out, not_2_out, not_3_out;
  wire [7:0] register_1_q;

  not not_1 (not_1_out, A);
  not not_2 (not_2_out, B);
  not not_3 (not_3_out, C);
  inv inv_1 (.in_1(in_2), .out_2(inv_1_out_2));
  and2 and2_1 (.in_1(not_1_out), .in_2(not_2_out), .out_3(and2_1_out_3));
  and2 and2_2 (.in_1(C), .in_2(not_2_out), .out_3(and2_2_out_3));
  and2 and2_3 (.in_1(not_3_out), .in_2(B), .out_3(and2_3_out_3));
  and2 and2_4 (.in_1(A), .in_2(B), .out_3(and2_4_out_3));
  and2 and2_5 (.in_1(not_1_out), .in_2(not_2_out), .out_3(and2_5_out_3));
  and2 and2_6 (.in_1(C), .in_2(not_2_out), .out_3(and2_6_out_3));
  and2 and2_7 (.in_1(C), .in_2(B), .out_3(and2_7_out_3));
  and2 and2_8 (.in_1(A), .in_2(B), .out_3(and2_8_out_3));
  Register register_1 (.D(in_1), .en(inv_1_out_2), .clk(in_3), .Q(register_1_q), .clr(in_4));
  and2 and2_9 (.in_1(not_3_out), .in_2(and2_1_out_3), .out_3(and2_9_out_3));
  and2 and2_10 (.in_1(not_1_out), .in_2(and2_2_out_3), .out_3(and2_10_out_3));
  and2 and2_11 (.in_1(not_1_out), .in_2(and2_3_out_3), .out_3(and2_11_out_3));
  and2 and2_12 (.in_1(C), .in_2(and2_4_out_3), .out_3(and2_12_out_3));
  and2 and2_13 (.in_1(C), .in_2(and2_5_out_3), .out_3(and2_13_out_3));
  and2 and2_14 (.in_1(not_1_out), .in_2(and2_6_out_3), .out_3(and2_14_out_3));
  and2 and2_15 (.in_1(not_1_out), .in_2(and2_7_out_3), .out_3(and2_15_out_3));
  and2 and2_16 (.in_1(C), .in_2(and2_8_out_3), .out_3(and2_16_out_3));
  sigif sigif_1 (.sig(register_1_q[7]), .cond(and2_9_out_3), .out_3(out_8));
  sigif sigif_2 (.sig(register_1_q[6]), .cond(and2_10_out_3), .out_3(out_8));
  sigif sigif_3 (.sig(register_1_q[5]), .cond(and2_11_out_3), .out_3(out_8));
  sigif sigif_4 (.sig(register_1_q[4]), .cond(and2_12_out_3), .out_3(out_8));
  sigif sigif_5 (.sig(register_1_q[3]), .cond(and2_13_out_3), .out_3(out_8));
  sigif sigif_6 (.sig(register_1_q[2]), .cond(and2_14_out_3), .out_3(out_8));
  sigif sigif_7 (.sig(register_1_q[1]), .cond(and2_15_out_3), .out_3(out_8));
  sigif sigif_8 (.sig(register_1_q[0]), .cond(and2_16_out_3), .out_3(out_8));

  // Notes on the sheet:
  //   0 0 1
  //   1 0 1
  //   0 0 0
  //   0 1 0
  //   0 1 1
  //   1 0 0
  //   1 1 0
  //   1 1 1
endmodule

module fpga_cell2_2d (
  input  N,
  input  [7:0] F,
  input  CS,
  input  ITM,
  input  CSR,
  input  E,
  input  W,
  input  S,
  output NO,
  output EO,
  output [7:0] FO,
  output WO,
  output CSO,
  output ITY,
  output CSRO,
  output SO
);

  wire fpga_cell2_2_cso, fpga_cell2_2_csro, fpga_cell2_2_ity, fpga_cell2_3_cso, fpga_cell2_3_csro,
       fpga_cell2_3_ity, fpga_cell2_4_cso, fpga_cell2_4_csro, fpga_cell2_4_ity;
  wire [7:0] fpga_cell2_2_fo, fpga_cell2_3_fo, fpga_cell2_4_fo;

  fpga_cell2 fpga_cell2_1 (
    .A(N), .B(E), .C(S), .F(fpga_cell2_2_fo), .CS(fpga_cell2_2_cso), .ITM(fpga_cell2_2_ity),
    .CSR(fpga_cell2_2_csro), .FO(FO), .R(WO), .CSO(CSO), .ITY(ITY), .CSRO(CSRO));
  fpga_cell2 fpga_cell2_2 (
    .A(W), .B(N), .C(E), .F(fpga_cell2_4_fo), .CS(fpga_cell2_4_cso), .ITM(fpga_cell2_4_ity),
    .CSR(fpga_cell2_4_csro), .FO(fpga_cell2_2_fo), .R(SO), .CSO(fpga_cell2_2_cso), .ITY(fpga_cell2_2_ity),
    .CSRO(fpga_cell2_2_csro));
  fpga_cell2 fpga_cell2_3 (
    .A(E), .B(S), .C(W), .F(F), .CS(CS), .ITM(ITM), .CSR(CSR), .FO(fpga_cell2_3_fo), .R(NO),
    .CSO(fpga_cell2_3_cso), .ITY(fpga_cell2_3_ity), .CSRO(fpga_cell2_3_csro));
  fpga_cell2 fpga_cell2_4 (
    .A(S), .B(W), .C(N), .F(fpga_cell2_3_fo), .CS(fpga_cell2_3_cso), .ITM(fpga_cell2_3_ity),
    .CSR(fpga_cell2_3_csro), .FO(fpga_cell2_4_fo), .R(EO), .CSO(fpga_cell2_4_cso), .ITY(fpga_cell2_4_ity),
    .CSRO(fpga_cell2_4_csro));
endmodule

module fpga (
);

  wire fpga_cell2_2d_1_cso, fpga_cell2_2d_1_csro, fpga_cell2_2d_1_eo, fpga_cell2_2d_1_ity,
       fpga_cell2_2d_1_so, fpga_cell2_2d_2_eo, fpga_cell2_2d_4_cso, fpga_cell2_2d_4_csro, fpga_cell2_2d_4_eo,
       fpga_cell2_2d_4_ity, fpga_cell2_2d_4_so, fpga_cell2_2d_5_eo, fpga_cell2_2d_5_so, fpga_cell2_2d_8_eo,
       undriven, undriven_2, undriven_3;

  fpga_cell2_2d fpga_cell2_2d_1 (
    .CS(undriven), .ITM(undriven_2), .CSR(undriven_3), .EO(fpga_cell2_2d_1_eo), .CSO(fpga_cell2_2d_1_cso),
    .ITY(fpga_cell2_2d_1_ity), .CSRO(fpga_cell2_2d_1_csro), .SO(fpga_cell2_2d_1_so));  // open: N, F, E, W, S, NO, FO, WO
  fpga_cell2_2d fpga_cell2_2d_2 (
    .N(fpga_cell2_2d_1_so), .EO(fpga_cell2_2d_2_eo));  // open: F, CS, ITM, CSR, E, W, S, NO, FO, WO, CSO, ITY, CSRO, SO
  fpga_cell2_2d fpga_cell2_2d_3 ();  // open: N, F, CS, ITM, CSR, E, W, S, NO, EO, FO, WO, CSO, ITY, CSRO, SO
  fpga_cell2_2d fpga_cell2_2d_4 (
    .CS(fpga_cell2_2d_1_cso), .ITM(fpga_cell2_2d_1_ity), .CSR(fpga_cell2_2d_1_csro), .W(fpga_cell2_2d_1_eo),
    .EO(fpga_cell2_2d_4_eo), .CSO(fpga_cell2_2d_4_cso), .ITY(fpga_cell2_2d_4_ity),
    .CSRO(fpga_cell2_2d_4_csro), .SO(fpga_cell2_2d_4_so));  // open: N, F, E, S, NO, FO, WO
  fpga_cell2_2d fpga_cell2_2d_5 (
    .N(fpga_cell2_2d_4_so), .W(fpga_cell2_2d_2_eo), .EO(fpga_cell2_2d_5_eo), .SO(fpga_cell2_2d_5_so));  // open: F, CS, ITM, CSR, E, S, NO, FO, WO, CSO, ITY, CSRO
  fpga_cell2_2d fpga_cell2_2d_6 (.N(fpga_cell2_2d_5_so));  // open: F, CS, ITM, CSR, E, W, S, NO, EO, FO, WO, CSO, ITY, CSRO, SO
  fpga_cell2_2d fpga_cell2_2d_7 ();  // open: N, F, CS, ITM, CSR, E, W, S, NO, EO, FO, WO, CSO, ITY, CSRO, SO
  fpga_cell2_2d fpga_cell2_2d_8 (
    .W(fpga_cell2_2d_5_eo), .EO(fpga_cell2_2d_8_eo));  // open: N, F, CS, ITM, CSR, E, S, NO, FO, WO, CSO, ITY, CSRO, SO
  fpga_cell2_2d fpga_cell2_2d_9 ();  // open: N, F, CS, ITM, CSR, E, W, S, NO, EO, FO, WO, CSO, ITY, CSRO, SO
  fpga_cell2_2d fpga_cell2_2d_10 ();  // open: N, F, CS, ITM, CSR, E, W, S, NO, EO, FO, WO, CSO, ITY, CSRO, SO
  fpga_cell2_2d fpga_cell2_2d_11 ();  // open: N, F, CS, ITM, CSR, E, W, S, NO, EO, FO, WO, CSO, ITY, CSRO, SO
  fpga_cell2_2d fpga_cell2_2d_12 (.W(fpga_cell2_2d_8_eo));  // open: N, F, CS, ITM, CSR, E, S, NO, EO, FO, WO, CSO, ITY, CSRO, SO
endmodule
