// Logisim project universal_logic_gate.circ as structural Verilog: 2 circuits, main circuit main
module main (
  input  in_1,
  input  in_2,
  output out_3,
  output out_4
);

  logicunit logicunit_1 (.A(in_1), .B(in_2), .R(out_4));  // open: F, Sel
  logicunit logicunit_2 (.A(in_2), .B(in_1), .R(out_3));  // open: F, Sel

  // Notes on the sheet:
  //   todo: 2d map
endmodule

module logicunit (
  input  A,
  input  B,
  input  [3:0] F,
  input  Sel,
  output R
);

  wire and_1_out, and_2_out, and_3_out, and_4_out, not_1_out, not_2_out;
  wire [3:0] register_1_q;

  not not_1 (not_1_out, A);
  not not_2 (not_2_out, B);
  Register #(.width(4)) register_1 (.D(F), .en(Sel), .clk(Sel), .Q(register_1_q));  // open: clr
  and and_1 (and_1_out, not_1_out, not_2_out);
  Transistor #(.\type ("n")) transistor_1 (.in(register_1_q[3]), .out(R), .gate(and_1_out));
  and and_2 (and_2_out, A, not_2_out);
  and and_3 (and_3_out, not_1_out, B);
  Transistor #(.\type ("n")) transistor_2 (.in(register_1_q[2]), .out(R), .gate(and_3_out));
  and and_4 (and_4_out, A, B);
  Transistor #(.\type ("n")) transistor_3 (.in(register_1_q[1]), .out(R), .gate(and_2_out));
  Transistor #(.\type ("n")) transistor_4 (.in(register_1_q[0]), .out(R), .gate(and_4_out));
endmodule
